# Fritzing sketch hardware (saved by Fritzing 0.9.2b)
breadboards: 1

parts:
  Part1 = Arduino Pro Mini v13
  Espessif_Serial_Wifi_Modul_1 = ESP8266 ESP01 [part_number=ESP8266 package=THT]
  U2 = V_REG_LD1117VXX [package=78xxl]
  C1 = Electrolytic Capacitor [capacitance=1mF package="100 mil [THT, electrolytic]"]
  C2 = Electrolytic Capacitor [capacitance=10µF package="100 mil [THT, electrolytic]"]
  VCC1 = LC-R121R3P
  R1 = Resistor [tolerance=±5% resistance=4.7k package=THT]
  R3 = Resistor [tolerance=±5% resistance=4.7k package=THT]
  R4 = Resistor [tolerance=±5% resistance=4.7k package=THT]

nets:
  N1: Part1.VCC, U2.IN, C2.+
  GND: Part1.GND, U2.GND, C2.-, VCC1.pin2
  N2: Part1.RAW, VCC1.pin1
  N3: Part1.D8, Espessif_Serial_Wifi_Modul_1.TXD
  N4: Part1.D7, R1.Pin_0
  N5: Espessif_Serial_Wifi_Modul_1.GND, C1.-, R4.Pin_0
  N6: Espessif_Serial_Wifi_Modul_1.RXD, R1.Pin_1, R3.Pin_0
  N7: Espessif_Serial_Wifi_Modul_1.VCC, Espessif_Serial_Wifi_Modul_1.CH_PD, U2.OUT, C1.+
  N8: R3.Pin_1, R4.Pin_1

custom parts:
  ESP8266 ESP01: Generic WiFi Module based on the ESP8266 with onboard PCB antenna and UART communications
  LC-R121R3P: 12V 1.Ah battery
